# Fritzing sketch whaletalk-device-fritzing (saved by Fritzing 0.9.4)

parts:
  Part1 = Adafruit MAX98357A I2S 3W Class D Amplifier [part_number="Adafruit #3006"]
  MCU1 = Raspberry Pi Zero
  SP1 = SPEAKER [package=pcb_mount_speaker]
  X1 = USB Connectors [package=usb-a-s-silk-female]
  R1 = Rotary Potentiometer (Large) [maximum_resistance=100kΩ package=THT]
  U1 = 74HC595 SMD [package="SO16 [SMD]"]  # not connected

nets:
  N1: Part1.VIN, MCU1.pin_4, X1.VBUS
  GND: Part1.GND, MCU1.pin_6, MCU1.pin_34, X1.GND
  N2: Part1.DIN, MCU1.pin_40
  N3: Part1.BCLK, MCU1.pin_12
  N4: Part1.LRCLK, MCU1.pin_35
  N5: Part1.VO-, R1.leg1
  N6: Part1.VO+, SP1.+
  N7: SP1.-, R1.wiper

custom parts:
  Adafruit MAX98357A I2S 3W Class D Amplifier: Listen to this good news - we now have an all in one digital audio amp breakout board that works incredibly well with the Raspberry Pi! If you're looking for an easy and low cost way to get you digital sound files bumpin' then the MAX08357 I2S Amp Breakout is for you. It takes standard I2S digital audio input and, not only decodes it into analog, but also amplifies it directly into a speaker.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
